// Logisim project intro.circ as structural Verilog: 1 circuit, main circuit main
module main (
  input  in_1,
  input  in_2,
  input  in_3,
  input  in_4,
  input  in_5,
  input  in_6,
  input  in_7,
  input  in_8,
  input  in_9,
  input  in_10,
  input  in_11,
  input  in_12,
  input  in_13,
  input  in_14,
  input  NOR,
  output out_16,
  output out_17,
  output out_18,
  output out_19,
  output out_20,
  output out_21,
  output out_22
);

  wire and_2_out, and_3_out;

  and and_1 (out_18, in_5, in_8);
  nand nand_1 (out_21, in_12, in_14);
  and and_2 (and_2_out, in_2, in_3);
  and and_3 (and_3_out, and_2_out, in_4);
  or or_1 (out_19, in_6, in_9);
  nor nor_1 (out_22, in_13, NOR);
  xor xor_1 (out_16, in_1, and_3_out);
  not not_1 (out_17, in_7);
  xor xor_2 (out_20, in_10, in_11);

  // Notes on the sheet:
  //   AND
  //   NAND
  //   OR
  //   NOT
  //   XOR
endmodule
